// Logisim project A1_Group1_Full.circ as structural Verilog: 1 circuit, main circuit main
module main (
  input  cs2,
  input  cs1,
  input  cs0,
  input  a3,
  input  a2,
  input  a1,
  input  a0,
  input  b3,
  input  b2,
  input  b1,
  input  b0,
  output C,
  output S,
  output V,
  output Z,
  output s3,
  output s2,
  output s1,
  output s0
);

  wire n7400_1_p2, n7400_1_p3, n7400_1_p4, n7400_1_p5, n7400_1_p6, n7400_1_p7, n7400_1_p8, n7400_1_p9,
       n7400_1_p10, n7400_1_p12, n7408_1_p2, n7408_1_p3, n7408_1_p8, n7408_1_p9, n7432_1_p2, n7432_1_p3,
       n7432_1_p4, n7432_1_p8, n7486_1_p2, n7486_1_p3, n7486_1_p7, n7486_1_p12, n74157_1_p2, n74157_1_p3,
       n74157_1_p6, n74157_1_p7, n74157_1_p8, n74157_1_p9, n74157_1_p12, n74157_1_p13, n74157_2_p7,
       n74157_2_p12, n74157_2_p13, n74157_3_p3, n74157_3_p8, n74157_3_p9;

  // Probe on n7400_1_p9
  // Probe on n7400_1_p8
  // Probe on n7432_1_p3
  // Probe on n7400_1_p7
  // Probe on n7400_1_p3
  // _7400 7400_1: pin names not known; wires that end beside it: 1'b0, n7400_1_p2, n7400_1_p3, n7400_1_p4, n7400_1_p5, n7400_1_p6, n7400_1_p7, n7400_1_p8, n7400_1_p9, n7400_1_p10, cs0, n7400_1_p12, cs0, 1'b1, 1'b0, n7400_1_p12
  // _7432 7432_1: pin names not known; wires that end beside it: 1'b0, n7432_1_p2, n7432_1_p3, n7432_1_p4, n7400_1_p2, s1, n7400_1_p8, n7432_1_p8, n7432_1_p4, n7432_1_p2, s2, s0, S, 1'b1
  // _74138 74138_1: pin names not known; wires that end beside it: n7400_1_p10, n7400_1_p7, 1'b1, 1'b0, 1'b0, n7400_1_p4, cs2, n7400_1_p5, cs1, n7400_1_p6, cs0, 1'b1
  // _7486 7486_1: pin names not known; wires that end beside it: 1'b0, n7486_1_p2, n7486_1_p3, n7486_1_p3, C, a3, n7486_1_p7, V, Z, n7486_1_p2, n7432_1_p8, n7486_1_p12, 1'b1, 1'b1
  // _7408 7408_1: pin names not known; wires that end beside it: 1'b0, n7408_1_p2, n7408_1_p3, b3, a1, a3, b1, n7408_1_p8, n7408_1_p9, a2, a0, b2, b0, 1'b1
  // _74157 74157_1: pin names not known; wires that end beside it: 1'b0, n74157_1_p2, n74157_1_p3, n7408_1_p2, n7408_1_p3, n74157_1_p6, n74157_1_p7, n74157_1_p8, n74157_1_p9, n7408_1_p8, n7408_1_p9, n74157_1_p12, n74157_1_p13, 1'b0, n7400_1_p7, 1'b1
  // _7486 7486_2: pin names not known; wires that end beside it: 1'b0, n74157_1_p6, n74157_1_p7, b3, a1, a3, b1, n74157_1_p12, n74157_1_p13, a2, a0, b2, b0, 1'b1
  // _74157 74157_2: pin names not known; wires that end beside it: 1'b0, S, s1, n74157_1_p2, n74157_1_p3, n7486_1_p7, n74157_2_p7, s2, s0, n74157_1_p8, n74157_1_p9, n74157_2_p12, n74157_2_p13, 1'b0, n7400_1_p3, 1'b1
  // _74157 74157_3: pin names not known; wires that end beside it: 1'b0, n7486_1_p12, n74157_3_p3, b3, b1, n7400_1_p9, n7400_1_p9, n74157_3_p8, n74157_3_p9, b2, b0, n7400_1_p9, n7400_1_p9, 1'b0, n7432_1_p3, 1'b1
  // _7483 7483_1: pin names not known; wires that end beside it: a1, n74157_2_p13, n74157_3_p3, a0, n74157_2_p7, n74157_3_p9, 1'b1, 1'b0, n74157_3_p8, n7400_1_p8, a2, C, n74157_2_p12, n7486_1_p7, a3, n7486_1_p12

  assign s3 = S;
endmodule
