// Logisim project A1_Group1_Modular.circ as structural Verilog: 6 circuits, main circuit Main
// Logical
module Logic_Unit (
  input  A3,
  input  A2,
  input  A1,
  input  A0,
  input  B3,
  input  B2,
  input  B1,
  input  B0,
  input  S1,
  output O3,
  output O2,
  output O1,
  output O0
);

  wire n7408_1_p3, n7408_1_p6, n7408_1_p11, n7408_1_p14, n7486_1_p3, n7486_1_p6, n7486_1_p11, n7486_1_p14;

  // _7486 7486_1: pin names not known; wires that end beside it: A3, B3, n7486_1_p3, A2, B2, n7486_1_p6, 1'b0, 1'b1, B0, A0, n7486_1_p11, B1, A1, n7486_1_p14
  // _7408 7408_1: pin names not known; wires that end beside it: A3, B3, n7408_1_p3, A2, B2, n7408_1_p6, 1'b0, 1'b1, B1, A1, n7408_1_p11, B0, A0, n7408_1_p14
  // _74157 74157_1: pin names not known; wires that end beside it: S1, n7486_1_p3, n7408_1_p3, O3, n7486_1_p6, n7408_1_p6, O2, 1'b0, 1'b1, 1'b0, n7486_1_p11, n7408_1_p14, O0, n7486_1_p14, n7408_1_p11, O1
endmodule

// Arithmetic
module Arithmetic_Unit (
  input  A3,
  input  A2,
  input  A1,
  input  A0,
  input  B3,
  input  B2,
  input  B1,
  input  B0,
  input  C,
  input  S0,
  input  Cin,
  output Cout,
  output O3,
  output O2,
  output O1,
  output O0,
  output I3
);

  wire input_for_au_1_o0, input_for_au_1_o1, input_for_au_1_o2;

  Input_for_AU input_for_au_1 (
    .B3(B3), .B2(B2), .B1(B1), .B0(B0), .C(C), .S0(S0), .O3(I3), .O2(input_for_au_1_o2),
    .O1(input_for_au_1_o1), .O0(input_for_au_1_o0));
  // _7483 7483_1: pin names not known; wires that end beside it: A3, O2, A2, input_for_au_1_o2, 1'b1, O1, input_for_au_1_o1, A1, I3, O3, Cout, Cin, 1'b0, input_for_au_1_o0, A0, O0
endmodule

// Input Proc
module Input_for_AU (
  input  B3,
  input  B2,
  input  B1,
  input  B0,
  input  C,
  input  S0,
  output O3,
  output O2,
  output O1,
  output O0
);

  // _74157 74157_1: pin names not known; wires that end beside it: S0, C, B3, O3, C, B2, O2, 1'b0, 1'b1, 1'b0, C, B0, O0, C, B1, O1
endmodule

module Combined (
  input  A3,
  input  A2,
  input  A1,
  input  A0,
  input  B3,
  input  B2,
  input  B1,
  input  B0,
  input  C,
  input  S0,
  input  S1,
  input  Cin,
  input  S2,
  output Cout,
  output O3,
  output O2,
  output O1,
  output O0,
  output S3,
  output I3
);

  wire arithmetic_unit_1_o0, arithmetic_unit_1_o1, arithmetic_unit_1_o2, logic_unit_1_o0, logic_unit_1_o1,
       logic_unit_1_o2, logic_unit_1_o3;

  Logic_Unit logic_unit_1 (
    .A3(A3), .A2(A2), .A1(A1), .A0(A0), .B3(B3), .B2(B2), .B1(B1), .B0(B0), .S1(S1), .O3(logic_unit_1_o3),
    .O2(logic_unit_1_o2), .O1(logic_unit_1_o1), .O0(logic_unit_1_o0));
  Arithmetic_Unit arithmetic_unit_1 (
    .A3(A3), .A2(A2), .A1(A1), .A0(A0), .B3(B3), .B2(B2), .B1(B1), .B0(B0), .C(C), .S0(S0), .Cin(Cin),
    .Cout(Cout), .O3(S3), .O2(arithmetic_unit_1_o2), .O1(arithmetic_unit_1_o1), .O0(arithmetic_unit_1_o0),
    .I3(I3));
  // _74157 74157_1: pin names not known; wires that end beside it: S2, S3, logic_unit_1_o3, O3, arithmetic_unit_1_o2, logic_unit_1_o2, O2, 1'b0, 1'b1, 1'b0, arithmetic_unit_1_o0, logic_unit_1_o0, O0, arithmetic_unit_1_o1, logic_unit_1_o1, O1
endmodule

module ALU (
  input  A3,
  input  A2,
  input  A1,
  input  A0,
  input  B3,
  input  B2,
  input  B1,
  input  B0,
  input  CS2,
  input  CS1,
  input  CS0,
  output C,
  output S,
  output V,
  output Z,
  output O3,
  output O2,
  output O1,
  output O0
);

  wire combined_1_i3, combined_1_s3, n7400_1_p3, n7400_1_p6, n7400_1_p11, n7400_1_p14, n7432_1_p3,
       n7432_1_p6, n7432_1_p11, n7432_1_p14, n7486_1_p3, n7486_1_p6, n74138_1_p7, n74138_1_p10, n74138_1_p11,
       n74138_1_p12, n74138_1_p13, n74138_1_p14;

  // _74138 74138_1: pin names not known; wires that end beside it: CS0, CS1, CS2, 1'b0, 1'b0, 1'b1, n74138_1_p7, 1'b0, 1'b1, n74138_1_p10, n74138_1_p11, n74138_1_p12, n74138_1_p13, n74138_1_p14
  // _7400 7400_1: pin names not known; wires that end beside it: CS0, CS0, n7400_1_p3, n74138_1_p14, n74138_1_p7, n7400_1_p6, 1'b0, 1'b1, n74138_1_p10, n74138_1_p12, n7400_1_p11, n74138_1_p11, n74138_1_p13, n7400_1_p14
  Combined combined_1 (
    .A3(A3), .A2(A2), .A1(A1), .A0(A0), .B3(B3), .B2(B2), .B1(B1), .B0(B0), .C(n7400_1_p3), .S0(n7432_1_p3),
    .S1(n74138_1_p13), .Cin(n7400_1_p6), .S2(n7400_1_p14), .Cout(C), .O3(O3), .O2(O2), .O1(O1), .O0(O0),
    .S3(combined_1_s3), .I3(combined_1_i3));
  // _7432 7432_1: pin names not known; wires that end beside it: n7400_1_p6, n7400_1_p11, n7432_1_p3, O3, O2, n7432_1_p6, 1'b0, 1'b1, n7432_1_p6, O1, n7432_1_p11, n7432_1_p11, O0, n7432_1_p14
  // _7486 7486_1: pin names not known; wires that end beside it: combined_1_s3, C, n7486_1_p3, n7486_1_p3, A3, n7486_1_p6, 1'b0, 1'b1, n7486_1_p6, combined_1_i3, V, n7432_1_p14, 1'b1, Z

  assign S = O3;
endmodule

module Main (
  input  A3,
  input  A2,
  input  A1,
  input  A0,
  input  B3,
  input  B2,
  input  B1,
  input  B0,
  input  CS2,
  input  CS1,
  input  CS0,
  output C,
  output S,
  output V,
  output Z,
  output O3,
  output O2,
  output O1,
  output O0
);

  ALU alu_1 (
    .A3(A3), .A2(A2), .A1(A1), .A0(A0), .B3(B3), .B2(B2), .B1(B1), .B0(B0), .C(C), .S(S), .V(V), .Z(Z),
    .CS2(CS2), .CS1(CS1), .CS0(CS0), .O3(O3), .O2(O2), .O1(O1), .O0(O0));
endmodule
